# Fritzing sketch emulator_dummy (saved by Fritzing 0.9.5d)

parts:
  元件1 = Arduino Uno (Rev3) - ICSP
  LCD1 = LCD screen  # not connected
  Grove1 = Grove OLED 128x96

nets:
  N1: 元件1.A4/SDA, Grove1.SDA
  N2: 元件1.A5/SCL, Grove1.SCL
  5V: 元件1.5V, Grove1.VCC
  GND: 元件1.GND, Grove1.GND
